// Logisim project LC2200.circ as structural Verilog: 2 circuits, main circuit main
module main (
);

  wire ALUHi, ALULo, chkZ, Clk, Clr, comparator_1_eq, comparator_2_eq, DrALU, DrMEM, DrOFF, DrPC, DrREG, LdA,
       LdB, LdIR, LdMAR, LdPC, LdZ, not_1_out, OPTest, RegSelHi, RegSelLo, WrMEM, WrREG, Z;
  wire [1:0] bit_extender_1_out;
  wire [2:0] OP;
  wire [3:0] RegNo, RX, RY, RZ;
  wire [4:4] IR_q;
  wire [5:0] multiplexer_1_out, register_1_q, rom_1_data, rom_2_data, State;
  wire [15:0] A_q, alu_1_out, and_1_out, B_q, bit_extender_2_out, bit_extender_3_out,
       controlled_buffer_1_out, MAR_q, PC_q, ram_1_data, ram_2_data;

  Register #(.width(16)) PC (.D(controlled_buffer_1_out), .en(LdPC), .Q(PC_q), .clk(Clk), .clr(Clr));
  assign controlled_buffer_1_out = DrPC ? PC_q : 16'bz;  // Controlled_Buffer controlled_buffer_1
  assign bit_extender_1_out = {{1{1'b0}}, Z};  // Bit_Extender bit_extender_1
  Register #(.width(16)) A (.D(controlled_buffer_1_out), .en(LdA), .Q(A_q), .clk(Clk), .clr(Clr));
  ALU alu_1 (.A(A_q), .B(B_q), .func({ALUHi, ALULo}), .Out(alu_1_out));
  Register #(.width(16)) B (.D(controlled_buffer_1_out), .en(LdB), .Q(B_q), .clk(Clk), .clr(Clr));
  assign controlled_buffer_1_out = DrALU ? alu_1_out : 16'bz;  // Controlled_Buffer controlled_buffer_2
  ROM #(.addrWidth(3), .dataWidth(6)) rom_1 (.addr(OP), .data(rom_1_data));  // open: sel
  ROM #(.addrWidth(2), .dataWidth(6)) rom_2 (.addr(bit_extender_1_out), .data(rom_2_data));  // open: sel
  Comparator #(.width(4)) comparator_1 (.a(4'b0000), .b(RegNo), .eq(comparator_1_eq));  // open: gt, lt
  Comparator #(.width(16)) comparator_2 (
    .a(controlled_buffer_1_out), .b({16{1'b0}}), .eq(comparator_2_eq));  // open: gt, lt
  Multiplexer #(.select(2), .width(6)) multiplexer_1 (
    .in0(State), .in1(rom_1_data), .in2(rom_2_data), .out(multiplexer_1_out), .sel({chkZ, OPTest}), .en(1'b1));  // open: in3
  not not_1 (not_1_out, comparator_1_eq);
  assign bit_extender_2_out = {{15{not_1_out}}, not_1_out};  // Bit_Extender bit_extender_2
  RAM #(.addrWidth(4), .dataWidth(16), .bus("separate")) ram_1 (
    .addr(RegNo), .din(controlled_buffer_1_out), .data(ram_1_data), .str(WrREG), .clk(Clk), .ld(1'b1),
    .clr(Clr));  // open: sel
  assign and_1_out = ram_1_data & bit_extender_2_out;  // AND_Gate and_1, 16 bits wide
  assign controlled_buffer_1_out = DrREG ? and_1_out : 16'bz;  // Controlled_Buffer controlled_buffer_3
  Register #(.width(1)) u_Z (.D(comparator_2_eq), .en(LdZ), .Q(Z), .clk(Clk), .clr(Clr));
  Register #(.width(6)) register_1 (.D(multiplexer_1_out), .Q(register_1_q), .clk(Clk), .clr(Clr));  // open: en
  Register #(.width(16)) MAR (.D(controlled_buffer_1_out), .en(LdMAR), .Q(MAR_q), .clk(Clk), .clr(Clr));
  ROM #(.addrWidth(6), .dataWidth(25)) rom_3 (
    .addr(register_1_q),
    .data({chkZ, OPTest, ALUHi, ALULo, RegSelHi, RegSelLo, WrMEM, WrREG, LdZ, LdB, LdA, LdMAR, LdIR, LdPC, DrOFF, DrPC, DrALU, DrMEM, DrREG, State}));  // open: sel
  Register #(.width(16)) IR (
    .D(controlled_buffer_1_out), .en(LdIR), .Q({OP, RX, RY, IR_q[4], RZ}), .clk(Clk), .clr(Clr));
  RAM #(.addrWidth(16), .dataWidth(16), .bus("separate")) ram_2 (
    .addr(MAR_q), .din(controlled_buffer_1_out), .data(ram_2_data), .str(WrMEM), .clk(Clk), .ld(1'b1));  // open: sel, clr
  assign controlled_buffer_1_out = DrMEM ? ram_2_data : 16'bz;  // Controlled_Buffer controlled_buffer_4
  assign bit_extender_3_out = {{11{IR_q[4]}}, {IR_q[4], RZ}};  // Bit_Extender bit_extender_3
  assign controlled_buffer_1_out = DrOFF ? bit_extender_3_out : 16'bz;  // Controlled_Buffer controlled_buffer_5
  Clock clock_1 (.out(Clk));
  Button button_1 (.out(Clr));
  Multiplexer #(.select(2), .width(4)) multiplexer_2 (
    .in0(RX), .in1(RY), .in2(RZ), .out(RegNo), .sel({RegSelHi, RegSelLo}), .en(1'b1));  // open: in3

  // Notes on the sheet:
  //   contents of rom_1 (hex, n*v repeats v):
  //   3 6 9 c 10 17 14 16
  //   contents of rom_2 (hex, n*v repeats v):
  //   1e 1b
  //   Registers 16 x 16 bits
  //   Memory 65536 x 16 bit
  //   contents of rom_3 (hex, n*v repeats v):
  //   6201 1082 e00900 84044 108045 20100 84047 108048 220100 8404a 840b 20100 8404d 840e 210f 20080 84051
  //   8412 2113 40040 a0215 840 16 4058 88059 41011a 1000000 421c 841d 900
endmodule

module ALU (
  input  [15:0] A,
  input  [15:0] B,
  input  [1:0] func,
  output [15:0] Out
);

  wire [15:0] a_1, a_b, add, \nand ;

  assign \nand  = ~(A & B);  // NAND_Gate nand_1, 16 bits wide
  Adder #(.width(16)) adder_1 (.a(A), .b(B), .out(add));  // open: cin, cout
  Subtractor #(.width(16)) subtractor_1 (.a(A), .b(B), .out(a_b));  // open: bin, bout
  Adder #(.width(16)) adder_2 (.a(A), .b(16'h1), .out(a_1));  // open: cin, cout
  Multiplexer #(.select(2), .width(16)) multiplexer_1 (
    .in0(add), .in1(\nand ), .in2(a_b), .in3(a_1), .out(Out), .sel(func));  // open: en

  // Other names for the same wires on the sheet: select[1:0] = func
endmodule
